// Logisim project SynthBite16.circ as structural Verilog: 1 circuit, main circuit SynthBite16
// Micro-Instruction number
module SynthBite16 (
  input  [15:0] in_1,
  input  [15:0] in_2,
  input  in_3,
  input  in_4,
  input  in_5,
  input  in_6
);

  wire AC_p2, AC_p3, AC_p18, AC_p19, AC_p20, AC_p21, AC_p22, AC_p23, AC_p24, AC_p25, AC_p26, AC_p27, AC_p28,
       AC_p29, adder_1_cout, adder_2_cout, and_2_out, and_4_out, and_7_out, and_8_out, and_9_out, and_10_out,
       button_1_out, button_2_out, carry_q, comparator_1_eq, comparator_1_gt, comparator_1_lt,
       decoder_1_out0, decoder_1_out1, decoder_1_out2, decoder_1_out4, decoder_1_out5, decoder_1_out6,
       decoder_1_out10, decoder_1_out11, decoder_1_out12, decoder_2_out0, decoder_2_out1, decoder_2_out3,
       decoder_2_out5, decoder_2_out6, decoder_2_out10, decoder_2_out11, decoder_2_out12, decoder_2_out13,
       decoder_2_out14, decoder_2_out15, demultiplexer_1_out0, demultiplexer_1_out1, demultiplexer_1_out2,
       demultiplexer_1_out3, demultiplexer_1_out4, demultiplexer_1_out5, demultiplexer_1_out6,
       demultiplexer_1_out7, IE_q, keyboard_1_avail, keyboard_2_avail, mAC_p2, MasterClock_out,
       multiplexer_8_out, nand_1_out, not_1_out, not_2_out, not_3_out, not_5_out, not_7_out, or_2_out,
       or_3_out, or_4_out, or_6_out, PC_carry, register_9_q, SP_carry, subtractor_1_bout, timing_sig_carry,
       undriven_3, undriven_4, undriven_5;
  wire [0:0] DR_q, not_6_out;
  wire [2:0] SP_q;
  wire [3:0] CWR_q_2, IR_q_2, IR_q_3, multiplexer_4_out;
  wire [5:5] and_3_out;
  wire [6:0] keyboard_1_data, outr_q_2;
  wire [7:0] CAR_q, IR_q, lookup_control_mem_address_for_instruction_data, multiplexer_3_out;
  wire [11:0] AR_q, controlled_buffer_3_out, PC_q;
  wire [15:0] adder_1_out, adder_2_out, adder_3_out, and_1_out, and_5_out, and_6_out,
       controlled_buffer_1_out, dAC_p18, DR_q_2, mAC_p1, multiplexer_1_out, multiplexer_2_out,
       multiplexer_5_out, multiplexer_6_out, multiplexer_7_out, not_4_out, or_1_out, rand_q, register_1_q,
       register_2_q, register_3_q, register_4_q, register_5_q, register_6_q, register_7_q, register_8_q,
       subtractor_1_out, subtractor_2_out, TR_q, undriven_2, xor_1_out, xor_2_out;
  wire [15:7] outr_q;
  wire [15:15] undriven;
  wire [31:0] CNTRL_MEM_data, CWR_q;

  LED led_1 (.in(MasterClock_out));
  Clock MasterClock (.out(MasterClock_out));
  Keyboard keyboard_1 (
    .clk(MasterClock_out), .re(1'b1), .clr(CWR_q[1]), .avail(keyboard_1_avail), .data(keyboard_1_data));
  Counter #(.max('h7), .width(3)) SP (
    .clr(button_1_out), .up(CWR_q[9]), .count(CWR_q[10]), .clk(MasterClock_out), .carry(SP_carry), .Q(SP_q));  // open: load, D
  assign controlled_buffer_1_out = decoder_1_out4 ? {IR_q_2, IR_q_3, IR_q} : 16'bz;  // Controlled_Buffer controlled_buffer_1
  assign controlled_buffer_1_out = decoder_1_out12 ? multiplexer_1_out : 16'bz;  // Controlled_Buffer controlled_buffer_2
  Multiplexer #(.select(3), .width(16)) multiplexer_1 (
    .in0(register_1_q), .in1(register_2_q), .in2(register_3_q), .in3(register_4_q), .in4(register_5_q),
    .in5(register_6_q), .in6(register_7_q), .in7(register_8_q), .out(multiplexer_1_out), .sel(SP_q));
  assign controlled_buffer_3_out = CWR_q[7] ? AR_q : 12'bz;  // Controlled_Buffer controlled_buffer_3
  Register #(.width(12)) AR (
    .D({IR_q[0], IR_q[1], IR_q[2], IR_q[3], IR_q[4], IR_q[5], IR_q[6], IR_q[7], IR_q_3[0], IR_q_3[1], IR_q_3[2], IR_q_3[3]}),
    .en(decoder_2_out5), .clk(MasterClock_out), .Q(AR_q), .clr(button_1_out));
  Register #(.trigger("falling"), .width(16)) DR (
    .D(controlled_buffer_1_out), .en(decoder_2_out10), .clk(MasterClock_out), .Q({DR_q_2[14:0], DR_q[0]}),
    .clr(button_1_out));
  Counter #(.max('hfff), .trigger("falling"), .width(12)) PC (
    .clr(button_1_out), .load(decoder_2_out3), .up(1'b1), .count(CWR_q[0]), .clk(MasterClock_out),
    .D({IR_q[0], IR_q[1], IR_q[2], IR_q[3], IR_q[4], IR_q[5], IR_q[6], IR_q[7], IR_q_3[0], IR_q_3[1], IR_q_3[2], IR_q_3[3]}),
    .carry(PC_carry), .Q(PC_q));
  DotMatrix #(.matrixcols(4), .matrixrows(1)) dotmatrix_1 (
    .col0(SP_carry), .col1(SP_carry), .col2(SP_carry), .col3(SP_carry));
  Demultiplexer #(.enable("true"), .select(3)) demultiplexer_1 (
    .out0(demultiplexer_1_out0), .out1(demultiplexer_1_out1), .out2(demultiplexer_1_out2),
    .out3(demultiplexer_1_out3), .out4(demultiplexer_1_out4), .out5(demultiplexer_1_out5),
    .out6(demultiplexer_1_out6), .out7(demultiplexer_1_out7), .in(1'b1), .sel(SP_q), .en(decoder_2_out15));
  assign controlled_buffer_1_out = decoder_1_out6 ? TR_q : 16'bz;  // Controlled_Buffer controlled_buffer_4
  Multiplexer #(.width(16)) multiplexer_2 (
    .in0({16{1'b1}}), .in1({{9{1'b0}}, keyboard_1_data}), .out(multiplexer_2_out), .sel(keyboard_1_avail));
  assign controlled_buffer_1_out = decoder_1_out5 ? multiplexer_2_out : 16'bz;  // Controlled_Buffer controlled_buffer_5
  Register #(.width(16)) register_1 (
    .D(controlled_buffer_1_out), .en(demultiplexer_1_out0), .clk(MasterClock_out), .Q(register_1_q),
    .clr(button_1_out));
  Register #(.width(16)) register_2 (
    .D(controlled_buffer_1_out), .en(demultiplexer_1_out1), .clk(MasterClock_out), .Q(register_2_q),
    .clr(button_1_out));
  Register #(.trigger("falling"), .width(16)) TR (
    .D(controlled_buffer_1_out), .en(decoder_2_out6), .clk(MasterClock_out), .Q(TR_q), .clr(button_1_out));
  Register #(.width(16)) register_3 (
    .D(controlled_buffer_1_out), .en(demultiplexer_1_out2), .clk(MasterClock_out), .Q(register_3_q),
    .clr(button_1_out));
  Register #(.width(16)) register_4 (
    .D(controlled_buffer_1_out), .en(demultiplexer_1_out3), .clk(MasterClock_out), .Q(register_4_q),
    .clr(button_1_out));
  DotMatrix #(.matrixcols(16), .matrixrows(1)) dotmatrix_2 (
    .col0(controlled_buffer_1_out[15]), .col1(controlled_buffer_1_out[14]),
    .col2(controlled_buffer_1_out[13]), .col3(controlled_buffer_1_out[12]),
    .col4(controlled_buffer_1_out[11]), .col5(controlled_buffer_1_out[10]),
    .col6(controlled_buffer_1_out[9]), .col7(controlled_buffer_1_out[8]), .col8(controlled_buffer_1_out[7]),
    .col9(controlled_buffer_1_out[6]), .col10(controlled_buffer_1_out[5]),
    .col11(controlled_buffer_1_out[4]), .col12(controlled_buffer_1_out[3]),
    .col13(controlled_buffer_1_out[2]), .col14(controlled_buffer_1_out[1]), .col15(controlled_buffer_1_out[0]));
  assign controlled_buffer_3_out = CWR_q[6] ? PC_q : 12'bz;  // Controlled_Buffer controlled_buffer_6
  Register #(.width(16)) register_5 (
    .D(controlled_buffer_1_out), .en(demultiplexer_1_out4), .clk(MasterClock_out), .Q(register_5_q),
    .clr(button_1_out));
  Register #(.width(16)) register_6 (
    .D(controlled_buffer_1_out), .en(demultiplexer_1_out5), .clk(MasterClock_out), .Q(register_6_q),
    .clr(button_1_out));
  Register #(.width(16)) register_7 (
    .D(controlled_buffer_1_out), .en(demultiplexer_1_out6), .clk(MasterClock_out), .Q(register_7_q),
    .clr(button_1_out));
  Register #(.width(16)) register_8 (
    .D(controlled_buffer_1_out), .en(demultiplexer_1_out7), .clk(MasterClock_out), .Q(register_8_q),
    .clr(button_1_out));
  Counter timing_sig (
    .clr(button_1_out), .up(CWR_q[0]), .count(1'b1), .carry(timing_sig_carry));  // open: load, clk, D, Q
  LED led_2 (.in(PC_carry));
  assign controlled_buffer_3_out = CWR_q[8] ? {IR_q[0], IR_q[1], IR_q[2], IR_q[3], IR_q[4], IR_q[5], IR_q[6], IR_q[7], IR_q_3[0], IR_q_3[1], IR_q_3[2], IR_q_3[3]} : 12'bz;  // Controlled_Buffer controlled_buffer_7
  Button button_1 (.out(button_1_out));
  LedBar #(.matrixcols(16)) ledbar_1 (
    .led0(IR_q_2[3]), .led1(IR_q_2[2]), .led2(IR_q_2[1]), .led3(IR_q_2[0]), .led4(IR_q_3[3]),
    .led5(IR_q_3[2]), .led6(IR_q_3[1]), .led7(IR_q_3[0]), .led8(IR_q[7]), .led9(IR_q[6]), .led10(IR_q[5]),
    .led11(IR_q[4]), .led12(IR_q[3]), .led13(IR_q[2]), .led14(IR_q[1]), .led15(IR_q[0]));
  // Probe on timing_sig_carry
  assign and_1_out = rand_q & controlled_buffer_1_out;  // AND_Gate and_1, 16 bits wide
  Register #(.width(16)) IR (
    .D(controlled_buffer_1_out), .en(decoder_2_out11), .clk(MasterClock_out), .Q({IR_q_2, IR_q_3, IR_q}),
    .clr(button_1_out));
  Adder #(.width(16)) adder_1 (
    .a({DR_q_2[14:0], DR_q[0]}), .b(controlled_buffer_1_out), .out(adder_1_out), .cin(DR_q_2[15]),
    .cout(adder_1_cout));
  assign xor_1_out = rand_q ^ and_1_out;  // XOR_Gate xor_1, 16 bits wide
  not not_1 (not_1_out, IR_q_2[2]);
  not not_2 (not_2_out, IR_q_2[1]);
  Subtractor #(.width(16)) subtractor_1 (
    .a({DR_q_2[14:0], DR_q[0]}), .b(controlled_buffer_1_out), .out(subtractor_1_out), .bin(DR_q_2[15]),
    .bout(subtractor_1_bout));
  assign or_1_out = controlled_buffer_1_out | {DR_q_2[14:0], DR_q[0]};  // OR_Gate or_1, 16 bits wide
  // Probe on rand_q
  TTY tty_1 (.data(outr_q_2), .clk(MasterClock_out), .we(decoder_2_out12), .clr(button_2_out));
  and and_2 (and_2_out, not_1_out, not_2_out);
  not not_3 (not_3_out, IR_q_2[0]);
  // Probe on controlled_buffer_1_out
  // Probe on controlled_buffer_3_out
  or or_2 (or_2_out, adder_1_cout, subtractor_1_bout);
  assign not_4_out = ~{DR_q_2[14:0], DR_q[0]};  // NOT_Gate not_4, 16 bits wide
  Register #(.width(16)) \rand  (.D(xor_1_out), .en(in_6), .clk(MasterClock_out), .Q(rand_q), .clr(button_1_out));
  and and_3 (and_3_out[5], and_2_out, not_3_out);
  Multiplexer #(.width(8)) multiplexer_3 (
    .in0(lookup_control_mem_address_for_instruction_data), .in1(8'hf9), .out(multiplexer_3_out),
    .sel(and_4_out));
  or or_3 (or_3_out, DR_q[0], adder_2_cout);
  assign xor_2_out = controlled_buffer_1_out ^ {DR_q_2[14:0], DR_q[0]};  // XOR_Gate xor_2, 16 bits wide
  and and_4 (and_4_out, keyboard_2_avail, IE_q);
  or or_4 (or_4_out, or_2_out, or_3_out);
  assign and_5_out = controlled_buffer_1_out & {DR_q_2[14:0], DR_q[0]};  // AND_Gate and_5, 16 bits wide
  assign and_6_out = {DR_q_2[14:0], DR_q[0]} & {16{undriven[15]}};  // AND_Gate and_6, 16 bits wide
  Adder #(.width(16)) adder_2 (.a(mAC_p1), .b(and_6_out), .out(adder_2_out), .cin(in_5), .cout(adder_2_cout));
  Button button_2 (.out(button_2_out));
  Multiplexer #(.width(4)) multiplexer_4 (.in0(IR_q_2), .in1(IR_q_3), .out(multiplexer_4_out), .sel(and_3_out[5]));
  // Shift_Register #(.length(16)) mAC: pin names not known; wires that end beside it: mAC_p1, mAC_p2, CWR_q[17], CWR_q[16], MasterClock_out, in_5
  Register #(.width(16)) outr (
    .D(controlled_buffer_1_out), .en(decoder_2_out12), .clk(MasterClock_out), .Q({outr_q, outr_q_2}),
    .clr(button_1_out));
  Register #(.width(1)) IE (.D(CWR_q[4]), .en(CWR_q[5]), .clk(MasterClock_out), .Q(IE_q), .clr(button_1_out));
  Adder #(.width(16)) adder_3 (.a(in_2), .b(controlled_buffer_1_out), .out(adder_3_out));  // open: cin, cout
  not not_5 (not_5_out, CWR_q[0]);
  Hex_Digit_Display #(.decimalPoint("false")) hex_digit_display_1 (.value(outr_q[15:12]));
  Hex_Digit_Display #(.decimalPoint("false")) hex_digit_display_2 (.value(outr_q[11:8]));
  ROM #(.addrWidth(6)) lookup_control_mem_address_for_instruction (
    .addr({and_3_out[5], IR_q_2[3], multiplexer_4_out}),
    .data(lookup_control_mem_address_for_instruction_data));
  Comparator #(.width(16)) comparator_1 (
    .a(controlled_buffer_1_out), .b({DR_q_2[14:0], DR_q[0]}), .gt(comparator_1_gt), .eq(comparator_1_eq),
    .lt(comparator_1_lt));
  Subtractor #(.width(16)) subtractor_2 (
    .a(dAC_p18), .b({DR_q_2[14:0], DR_q[0]}), .out(subtractor_2_out));  // open: bin, bout
  Hex_Digit_Display #(.decimalPoint("false")) hex_digit_display_3 (.value({outr_q[7], outr_q_2[6:4]}));
  Counter #(.trigger("falling")) CAR (
    .clr(button_1_out), .load(CWR_q[0]), .up(1'b1), .count(not_5_out), .clk(MasterClock_out),
    .D(multiplexer_3_out), .Q(CAR_q));  // open: carry
  or or_5 (mAC_p2, CWR_q[12], button_1_out);
  Multiplexer #(.width(16)) multiplexer_5 (
    .in0(subtractor_2_out), .in1(controlled_buffer_1_out), .out(multiplexer_5_out), .sel(and_7_out));
  assign controlled_buffer_1_out = decoder_1_out10 ? dAC_p18 : 16'bz;  // Controlled_Buffer controlled_buffer_8
  Hex_Digit_Display #(.decimalPoint("false")) hex_digit_display_4 (.value(outr_q_2[3:0]));
  and and_7 (and_7_out, and_8_out, CWR_q[17]);
  // Shift_Register #(.length(16)) dAC: pin names not known; wires that end beside it: mAC_p2, CWR_q[17], CWR_q[16], MasterClock_out, undriven_2[15], multiplexer_5_out[0], multiplexer_5_out[1], multiplexer_5_out[2], multiplexer_5_out[3], multiplexer_5_out[4], multiplexer_5_out[5], multiplexer_5_out[6], multiplexer_5_out[7], multiplexer_5_out[8], multiplexer_5_out[9], multiplexer_5_out[10], multiplexer_5_out[11], dAC_p18[0], dAC_p18[1], dAC_p18[2], dAC_p18[3], dAC_p18[4], dAC_p18[5], dAC_p18[6], dAC_p18[7], dAC_p18[8], dAC_p18[9], dAC_p18[10], dAC_p18[11]
  ROM #(.dataWidth(32)) CNTRL_MEM (.addr(CAR_q), .data(CNTRL_MEM_data));
  and and_8 (and_8_out, CWR_q[11], undriven_2[15]);
  Keyboard #(.buflen(7)) keyboard_2 (
    .clk(MasterClock_out), .re(1'b1), .clr(CWR_q[2]), .avail(keyboard_2_avail));  // open: data
  not not_6 (not_6_out[0], dAC_p18[15]);
  Multiplexer #(.width(16)) multiplexer_6 (
    .in0({undriven_2[15:1], not_6_out[0]}), .in1(controlled_buffer_1_out), .out(multiplexer_6_out),
    .sel(decoder_2_out14));
  Register #(.trigger("falling"), .width(32)) CWR (
    .D(CNTRL_MEM_data), .en(1'b1), .clk(MasterClock_out),
    .Q({CWR_q[31:24], CWR_q_2[0], CWR_q_2[1], CWR_q_2[2], CWR_q_2[3], CWR_q[19:0]}), .clr(button_1_out));
  Multiplexer #(.enable("true"), .select(4), .width(16)) multiplexer_7 (
    .in0({DR_q_2[14:0], DR_q[0]}), .in1(not_4_out), .in2(adder_1_out), .in3(subtractor_1_out),
    .in4(or_1_out), .in5(xor_2_out), .in6(and_5_out), .in7(DR_q_2), .in8(in_1), .in9(rand_q),
    .in10(adder_3_out), .in11(mAC_p1), .in12(dAC_p18), .in13(in_1), .in14(in_1), .in15(in_1),
    .out(multiplexer_7_out), .sel(CWR_q_2), .en(CWR_q[19]));
  // Shift_Register #(.length(16)) Q: pin names not known; wires that end beside it: button_1_out, CWR_q[11], CWR_q[16], MasterClock_out, in_4, multiplexer_6_out[0], multiplexer_6_out[1], multiplexer_6_out[2], multiplexer_6_out[3], multiplexer_6_out[4], multiplexer_6_out[5], multiplexer_6_out[6], multiplexer_6_out[7], multiplexer_6_out[8], multiplexer_6_out[9], multiplexer_6_out[10], multiplexer_6_out[11]
  DotMatrix #(.matrixcols(32), .matrixrows(1)) dotmatrix_3 (
    .col0(CWR_q[31]), .col1(CWR_q[30]), .col2(CWR_q[29]), .col3(CWR_q[28]), .col4(CWR_q[27]),
    .col5(CWR_q[26]), .col6(CWR_q[25]), .col7(CWR_q[24]), .col8(CWR_q_2[0]), .col9(CWR_q_2[1]),
    .col10(CWR_q_2[2]), .col11(CWR_q_2[3]), .col12(CWR_q[19]), .col13(CWR_q[18]), .col14(CWR_q[17]),
    .col15(CWR_q[16]), .col16(CWR_q[15]), .col17(CWR_q[14]), .col18(CWR_q[13]), .col19(CWR_q[12]),
    .col20(CWR_q[11]), .col21(CWR_q[10]), .col22(CWR_q[9]), .col23(CWR_q[8]), .col24(CWR_q[7]),
    .col25(CWR_q[6]), .col26(CWR_q[5]), .col27(CWR_q[4]), .col28(CWR_q[3]), .col29(CWR_q[2]),
    .col30(CWR_q[1]), .col31(CWR_q[0]));
  // Probe on multiplexer_7_out
  assign controlled_buffer_1_out = decoder_1_out11 ? undriven_2 : 16'bz;  // Controlled_Buffer controlled_buffer_9
  not not_7 (not_7_out, CWR_q_2[2]);
  nand nand_1 (nand_1_out, CWR_q_2[1], CWR_q_2[0]);
  and and_9 (and_9_out, not_7_out, nand_1_out);
  // Probe on controlled_buffer_3_out
  and and_10 (and_10_out, CWR_q_2[3], and_9_out);
  buf buffer_1 (CWR_q[13], or_4_out);
  Multiplexer #(.select(2)) multiplexer_8 (
    .in0(carry_q), .in1(comparator_1_lt), .in2(comparator_1_eq), .in3(comparator_1_gt),
    .out(multiplexer_8_out), .sel({CWR_q[14], CWR_q[15]}));
  // Shift_Register #(.length(16), .trigger("falling")) AC: pin names not known; wires that end beside it: button_1_out, AC_p2, AC_p3, MasterClock_out, DR_q_2[15], multiplexer_7_out[0], multiplexer_7_out[1], multiplexer_7_out[2], multiplexer_7_out[3], multiplexer_7_out[4], multiplexer_7_out[5], multiplexer_7_out[6], multiplexer_7_out[7], multiplexer_7_out[8], multiplexer_7_out[9], multiplexer_7_out[10], multiplexer_7_out[11], AC_p18, AC_p19, AC_p20, AC_p21, AC_p22, AC_p23, AC_p24, AC_p25, AC_p26, AC_p27, AC_p28, AC_p29
  RAM #(.addrWidth(12), .dataWidth(16), .databus("bidir"), .enables("line")) MEM (
    .addr(controlled_buffer_3_out), .we(decoder_2_out1), .oe(decoder_1_out1), .clk(MasterClock_out),
    .data(controlled_buffer_1_out));
  D_Flip_Flop carry (.D(or_4_out), .clk(MasterClock_out), .Q(carry_q), .reset(button_1_out));  // open: Qn, preset
  or or_6 (or_6_out, or_4_out, multiplexer_8_out);
  assign controlled_buffer_1_out[0] = decoder_1_out2 ? AC_p18 : 1'bz;  // Controlled_Buffer controlled_buffer_10
  assign controlled_buffer_1_out[1] = decoder_1_out2 ? AC_p19 : 1'bz;  // Controlled_Buffer controlled_buffer_11
  assign controlled_buffer_1_out[2] = decoder_1_out2 ? AC_p20 : 1'bz;  // Controlled_Buffer controlled_buffer_12
  assign controlled_buffer_1_out[3] = decoder_1_out2 ? AC_p21 : 1'bz;  // Controlled_Buffer controlled_buffer_13
  assign controlled_buffer_1_out[4] = decoder_1_out2 ? AC_p22 : 1'bz;  // Controlled_Buffer controlled_buffer_14
  assign controlled_buffer_1_out[5] = decoder_1_out2 ? AC_p23 : 1'bz;  // Controlled_Buffer controlled_buffer_15
  assign controlled_buffer_1_out[6] = decoder_1_out2 ? AC_p24 : 1'bz;  // Controlled_Buffer controlled_buffer_16
  assign controlled_buffer_1_out[7] = decoder_1_out2 ? AC_p25 : 1'bz;  // Controlled_Buffer controlled_buffer_17
  assign controlled_buffer_1_out[8] = decoder_1_out2 ? AC_p26 : 1'bz;  // Controlled_Buffer controlled_buffer_18
  assign controlled_buffer_1_out[9] = decoder_1_out2 ? AC_p27 : 1'bz;  // Controlled_Buffer controlled_buffer_19
  assign controlled_buffer_1_out[10] = decoder_1_out2 ? AC_p28 : 1'bz;  // Controlled_Buffer controlled_buffer_20
  assign controlled_buffer_1_out[11] = decoder_1_out2 ? AC_p29 : 1'bz;  // Controlled_Buffer controlled_buffer_21
  assign controlled_buffer_1_out[12] = decoder_1_out2 ? undriven_3 : 1'bz;  // Controlled_Buffer controlled_buffer_22
  assign controlled_buffer_1_out[13] = decoder_1_out2 ? undriven_4 : 1'bz;  // Controlled_Buffer controlled_buffer_23
  assign controlled_buffer_1_out[14] = decoder_1_out2 ? undriven_5 : 1'bz;  // Controlled_Buffer controlled_buffer_24
  assign controlled_buffer_1_out[15] = decoder_1_out2 ? undriven[15] : 1'bz;  // Controlled_Buffer controlled_buffer_25
  LED led_3 (.in(decoder_1_out0));
  Decoder #(.enable("false"), .select(4)) decoder_1 (
    .out0(decoder_1_out0), .out1(decoder_1_out1), .out2(decoder_1_out2), .out4(decoder_1_out4),
    .out5(decoder_1_out5), .out6(decoder_1_out6), .out10(decoder_1_out10), .out11(decoder_1_out11),
    .out12(decoder_1_out12), .sel(CWR_q[31:28]));  // open: out3, out7, out8, out9, out13, out14, out15
  LED led_4 (.in(decoder_2_out0));
  Decoder #(.enable("false"), .select(4)) decoder_2 (
    .out0(decoder_2_out0), .out1(decoder_2_out1), .out2(AC_p2), .out3(decoder_2_out3), .out5(decoder_2_out5),
    .out6(decoder_2_out6), .out10(decoder_2_out10), .out11(decoder_2_out11), .out12(decoder_2_out12),
    .out13(decoder_2_out13), .out14(decoder_2_out14), .out15(decoder_2_out15), .sel(CWR_q[27:24]));  // open: out4, out7, out8, out9
  Register #(.width(1)) register_9 (
    .D(or_6_out), .en(in_3), .clk(MasterClock_out), .Q(register_9_q), .clr(button_1_out));
  D_Flip_Flop d_ff_1 (
    .D(decoder_2_out13), .clk(MasterClock_out), .Q(DR_q_2[15]), .reset(button_1_out));  // open: Qn, preset
  or or_7 (AC_p3, and_10_out, CWR_q[18]);

  // Notes on the sheet:
  //   CLOCK
  //   INPUT(BUFFER)
  //   16 LINES
  //   ADDRESS BUS
  //   STACK OVERFLOW
  //   REGISTER STACK
  //   PRESENT BUS VALUES
  //   END OF THE LINE
  //   COARSE GRAINED TIMER, DEPENDS ON THE INSTRUCTIONS THAN MICRO-INSTRUCTIONS
  //   COMPUTER REBOOT
  //   ADDRESS BUS
  //   PRESENT INSTRUCTION
  //   GOTO INTERRUPT ADDRESS(IN CNTROL MEM)
  //   AC RESET ASYNC
  //   OP-CODE
  //   ADDRESSING MODE
  //   GENERAL SYSTEM BUS
  //   OUTPUT STREAM
  //   VALUE ON MAIN BUS
  //   VALUE ON ADDRESS BUS
  //   ADDRESS BUS
  //   NXT INSN FRM CNTRL MEM OR MEM
  //   SECOND NIBBLE NEEDED?
  //   CONTROL UNIT
  //   ALU
  //   LEAST SIGNIFICANT LINE
  //   OUTPUT
  //   ADDRESS BUS
  //   contents of lookup_control_mem_address_for_instruction (hex, n*v repeats v):
  //   0 0 4 8 7*0 16 44*0 d
  //   MOST SIGNIFICANT LINE
  //   contents of CNTRL_MEM (hex, n*v repeats v):
  //   1b000040 1a000101 0 0 b000040 21000001 0 0 b000040 50000040 13000081 0 0 1b000040 2000
  //   INTERRUPT
  //   ADDRESS BUS
  //   this line is just a place holder
  //   PRESENT CONTROL
  //   STACK POINTER VALUE MANIPULATE
  //   IR(4..=15) ON BUS(ADDRESS)
  //   AR ON BUS(ADDRESS)
  //   PC ON BUS(ADDRESS)
  //   ADDRESS BUS
  //   ACC SHIFT(L)
  //   NONE
  //   MEM OUT ENABLE
  //   ACC ON BUS
  //   INPUT ON BUS
  //   TMP ON BUS
  //   PUT ON BUS
  //   dAC ON BUS
  //   Q ON BUS
  //   STACK TOP ON BUS
  //   NONE
  //   TMP LOAD
  //   LOAD FROM BUS
  //   DR LOAD
  //   IR LOAD
  //   OUT LOAD
  //   SRL IN
  //   LOAD Q
  //   CONDITION
  //   CONDITION FLIP FLOP
  //   IR ON BUS(GENERAL)
  //   MEM WRITE ENABLE
  //   AC PARLLEL LOAD
  //   PC LOAD
  //   AR LOAD
  //   PUSH TO STACK
  //   SERIAL IN
endmodule
